// Logisim project BOB-2200.circ as structural Verilog: 7 circuits, main circuit my circuit
module my_circuit (
);

  wire CLK, CmpOut, CondType, DrALU, DrCmp, DrMEM, DrOFF, DrPC, DrREG, LdA, LdB, LdCmp, LdIR, LdMAR, LdPC,
       RST, WrMEM, WrREG;
  wire [1:0] Func, RegSel;
  wire [3:0] OPCode, regno;
  wire [23:0] MAR_final_addr;
  wire [27:0] IR_q;
  wire [31:0] A_q, ALU_output, B_q, CmpReg_q, Comparison_Logic_output, controlled_buffer_1_out, PC_q,
       Register_dout, Sign_Extension_offset;

  Clock clock_1 (.out(CLK));
  Register_part #(.width(32)) PC (.D(controlled_buffer_1_out), .en(LdPC), .Q(PC_q), .clk(CLK), .clr(RST));
  assign controlled_buffer_1_out = DrPC ? PC_q : 32'bz;  // Controlled_Buffer controlled_buffer_1
  Button button_1 (.out(RST));
  Register_part #(.width(32)) B (.D(controlled_buffer_1_out), .en(LdB), .Q(B_q), .clk(CLK), .clr(RST));
  Comparison_Logic Comparison_Logic (
    .Input(controlled_buffer_1_out), .CompType(CondType), .Output(Comparison_Logic_output));
  Register_part #(.width(32)) CmpReg (.D(Comparison_Logic_output), .en(LdCmp), .Q(CmpReg_q), .clk(CLK), .clr(RST));
  ALU ALU (.A(A_q), .B(B_q), .in_3(Func), .Output(ALU_output));
  assign controlled_buffer_1_out = DrALU ? ALU_output : 32'bz;  // Controlled_Buffer controlled_buffer_2
  assign controlled_buffer_1_out = DrCmp ? CmpReg_q : 32'bz;  // Controlled_Buffer controlled_buffer_3
  Register_part #(.width(32)) A (.D(controlled_buffer_1_out), .en(LdA), .Q(A_q), .clk(CLK), .clr(RST));
  Register Register (
    .CLK(CLK), .RST(RST), .Din(controlled_buffer_1_out), .WrREG(WrREG), .regno(regno), .Dout(Register_dout));
  assign controlled_buffer_1_out = DrREG ? Register_dout : 32'bz;  // Controlled_Buffer controlled_buffer_4
  BitSelector #(.width(32)) bitselector_1 (.in(Comparison_Logic_output), .out(CmpOut), .sel({5{1'b0}}));
  MAR MAR (.Addr(controlled_buffer_1_out), .LdMAR(LdMAR), .CLK(CLK), .RST(RST), .Final_Addr(MAR_final_addr));
  RAM #(.addrWidth(24), .dataWidth(32), .bus("separate")) ram_1 (
    .addr(MAR_final_addr), .din(controlled_buffer_1_out), .data(controlled_buffer_1_out), .str(WrMEM),
    .sel(1'b1), .clk(CLK), .ld(DrMEM), .clr(RST));
  Register_part #(.width(32)) IR (.D(controlled_buffer_1_out), .en(LdIR), .Q({OPCode, IR_q}), .clk(CLK), .clr(RST));
  Multiplexer #(.select(2), .width(4), .disabled(0), .enable("false")) multiplexer_1 (
    .in0(IR_q[27:24]), .in1(IR_q[23:20]), .in2(IR_q[3:0]), .out(regno), .sel(RegSel));  // open: in3
  Microcontroller microcontroller_1 (
    .CLK(CLK), .RST(RST), .OpCode(OPCode), .CompOut(CmpOut), .DrREG(DrREG), .DrMEM(DrMEM), .DrALU(DrALU),
    .DrPC(DrPC), .DrOFF(DrOFF), .LdPC(LdPC), .LdIR(LdIR), .LdMAR(LdMAR), .LdA(LdA), .LdB(LdB), .LdCmp(LdCmp),
    .WrREG(WrREG), .WrMEM(WrMEM), .RegSel(RegSel), .Func(Func), .DrCmp(DrCmp), .CondType(CondType));
  Sign_Extension Sign_Extension (.OpCode(OPCode), .IR({OPCode, IR_q}), .Offset(Sign_Extension_offset));
  assign controlled_buffer_1_out = DrOFF ? Sign_Extension_offset : 32'bz;  // Controlled_Buffer controlled_buffer_5
endmodule

module ALU (
  input  [31:0] A,
  input  [31:0] B,
  input  [1:0] in_3,
  output [31:0] Output
);

  wire [31:0] adder_1_out, adder_2_out, nand_1_out, subtractor_1_out;

  Adder #(.width(32)) adder_1 (.a(A), .b(B), .out(adder_1_out), .cin(1'b0));  // open: cout
  Subtractor #(.width(32)) subtractor_1 (.a(A), .b(B), .out(subtractor_1_out), .bin(1'b0));  // open: bout
  assign nand_1_out = ~(A & B);  // NAND_Gate nand_1, 32 bits wide
  Adder #(.width(32)) adder_2 (.a(A), .b(32'h1), .out(adder_2_out), .cin(1'b0));  // open: cout
  Multiplexer #(.select(2), .width(32), .disabled(0), .enable("false")) multiplexer_1 (
    .in0(adder_1_out), .in1(subtractor_1_out), .in2(nand_1_out), .in3(adder_2_out), .out(Output), .sel(in_3));
endmodule

module MAR (
  input  [31:0] Addr,
  input  LdMAR,
  input  CLK,
  input  RST,
  output [23:0] Final_Addr
);

  wire [31:24] MAR_q;

  Register_part #(.width(32)) MAR (.D(Addr), .en(LdMAR), .Q({MAR_q, Final_Addr}), .clk(CLK), .clr(RST));
endmodule

module Register (
  input  CLK,
  input  RST,
  input  [31:0] Din,
  input  WrREG,
  input  [3:0] regno,
  output [31:0] Dout
);

  wire a0, a1, a2, at, fp, k0, ra, s0, s1, s2, sp, t0, t1, t2, v0, zero;
  wire [31:0] a0_q, a1_q, a2_q, at_q, fp_q, k0_q, ra_q, s0_q, s1_q, s2_q, sp_q, t0_q, t1_q, t2_q, v0_q,
       zero_q;

  Demultiplexer #(.select(4), .disabled(0), .enable("false")) demultiplexer_1 (
    .out0(zero), .out1(at), .out2(v0), .out3(a0), .out4(a1), .out5(a2), .out6(t0), .out7(t1), .out8(t2),
    .out9(s0), .out10(s1), .out11(s2), .out12(k0), .out13(sp), .out14(fp), .out15(ra), .in(WrREG), .sel(regno));
  Register_part #(.width(32)) u_zero (.D({32{1'b0}}), .en(1'b0), .Q(zero_q), .clk(CLK), .clr(RST));
  Register_part #(.width(32)) u_a1 (.D(Din), .en(a1), .Q(a1_q), .clk(CLK), .clr(RST));
  Register_part #(.width(32)) u_t2 (.D(Din), .en(t2), .Q(t2_q), .clk(CLK), .clr(RST));
  Register_part #(.width(32)) u_k0 (.D(Din), .en(k0), .Q(k0_q), .clk(CLK), .clr(RST));
  Register_part #(.width(32)) u_at (.D(Din), .en(at), .Q(at_q), .clk(CLK), .clr(RST));
  Register_part #(.width(32)) u_a2 (.D(Din), .en(a2), .Q(a2_q), .clk(CLK), .clr(RST));
  Register_part #(.width(32)) u_s0 (.D(Din), .en(s0), .Q(s0_q), .clk(CLK), .clr(RST));
  Register_part #(.width(32)) u_sp (.D(Din), .en(sp), .Q(sp_q), .clk(CLK), .clr(RST));
  Register_part #(.width(32)) u_v0 (.D(Din), .en(v0), .Q(v0_q), .clk(CLK), .clr(RST));
  Register_part #(.width(32)) u_t0 (.D(Din), .en(t0), .Q(t0_q), .clk(CLK), .clr(RST));
  Register_part #(.width(32)) u_s1 (.D(Din), .en(s1), .Q(s1_q), .clk(CLK), .clr(RST));
  Register_part #(.width(32)) u_fp (.D(Din), .en(fp), .Q(fp_q), .clk(CLK), .clr(RST));
  Register_part #(.width(32)) u_a0 (.D(Din), .en(a0), .Q(a0_q), .clk(CLK), .clr(RST));
  Register_part #(.width(32)) u_t1 (.D(Din), .en(t1), .Q(t1_q), .clk(CLK), .clr(RST));
  Register_part #(.width(32)) u_s2 (.D(Din), .en(s2), .Q(s2_q), .clk(CLK), .clr(RST));
  Register_part #(.width(32)) u_ra (.D(Din), .en(ra), .Q(ra_q), .clk(CLK), .clr(RST));
  Multiplexer #(.select(4), .width(32), .disabled(0), .enable("false")) multiplexer_1 (
    .in0(zero_q), .in1(at_q), .in2(v0_q), .in3(a0_q), .in4(a1_q), .in5(a2_q), .in6(t0_q), .in7(t1_q),
    .in8(t2_q), .in9(s0_q), .in10(s1_q), .in11(s2_q), .in12(k0_q), .in13(sp_q), .in14(fp_q), .in15(ra_q),
    .out(Dout), .sel(regno));
endmodule

module Comparison_Logic (
  input  [31:0] Input,
  input  CompType,
  output [31:0] Output
);

  wire comparator_1_lt, comparator_2_eq, not_1_out;
  wire [31:0] bit_extender_1_out, bit_extender_2_out;

  Comparator #(.width(32)) comparator_1 (.a(Input), .b({32{1'b0}}), .lt(comparator_1_lt));  // open: gt, eq
  Comparator #(.width(32)) comparator_2 (.a(Input), .b({32{1'b0}}), .eq(comparator_2_eq));  // open: gt, lt
  assign bit_extender_1_out = {{31{1'b0}}, comparator_1_lt};  // Bit_Extender bit_extender_1
  assign bit_extender_2_out = {{31{1'b0}}, not_1_out};  // Bit_Extender bit_extender_2
  not not_1 (not_1_out, comparator_2_eq);
  Multiplexer #(.width(32), .disabled(0), .enable("false")) multiplexer_1 (
    .in0(bit_extender_1_out), .in1(bit_extender_2_out), .out(Output), .sel(CompType));
endmodule

module Microcontroller (
  input  CLK,
  input  RST,
  input  [3:0] OpCode,
  input  CompOut,
  output DrREG,
  output DrMEM,
  output DrALU,
  output DrPC,
  output DrOFF,
  output LdPC,
  output LdIR,
  output LdMAR,
  output LdA,
  output LdB,
  output LdCmp,
  output WrREG,
  output WrMEM,
  output [1:0] RegSel,
  output [1:0] Func,
  output DrCmp,
  output CondType
);

  wire ChkCmp, OPtest;
  wire [5:0] multiplexer_1_out, rom_1_data, rom_2_data, rom_3_data, State_Register_q;

  ROM #(.addrWidth(4), .dataWidth(6)) rom_1 (.addr(OpCode), .data(rom_1_data), .sel(1'b1));
  ROM #(.addrWidth(2), .dataWidth(6)) rom_2 (.addr({1'b0, CompOut}), .data(rom_2_data), .sel(1'b1));
  Multiplexer #(.select(2), .width(6), .disabled(0), .enable("false")) multiplexer_1 (
    .in0(rom_3_data), .in1(rom_1_data), .in2(rom_2_data), .out(multiplexer_1_out), .sel({ChkCmp, OPtest}));  // open: in3
  Register_part #(.width(6)) State_Register (
    .D(multiplexer_1_out), .en(1'b1), .Q(State_Register_q), .clk(CLK), .clr(RST));
  ROM #(.addrWidth(6), .dataWidth(27)) rom_3 (
    .addr(State_Register_q),
    .data({CondType, DrCmp, ChkCmp, OPtest, Func, RegSel, WrMEM, WrREG, LdCmp, LdB, LdA, LdMAR, LdIR, LdPC, DrOFF, DrPC, DrALU, DrMEM, DrREG, rom_3_data}),
    .sel(1'b1));

  // Notes on the sheet:
  //   contents of rom_1 (hex, n*v repeats v):
  //   3 6 9 c 10 14 1a 1c 1d 21
  //   contents of rom_2 (hex, n*v repeats v):
  //   0 17
  //   contents of rom_3 (hex, n*v repeats v):
  //   6201 1082 e00900 84044 108045 20100 84047 108048 420100 8404a 840b 20100 8404d 840e 210f 20080 84051
  //   8412 2113 40040 4055 88056 5210100 4218 8419 900 2021b 80840 1c 8405e 10805f 210120 2020000 4222
  //   8423 20100
endmodule

module Sign_Extension (
  input  [3:0] OpCode,
  input  [31:0] IR,
  output [31:0] Offset
);

  wire [31:0] bit_extender_1_out;

  assign bit_extender_1_out = {{12{IR[19]}}, IR[19:0]};  // Bit_Extender bit_extender_1
  Multiplexer #(.select(4), .width(32), .disabled(0), .enable("false")) multiplexer_1 (
    .in2(bit_extender_1_out), .in3(bit_extender_1_out), .in4(bit_extender_1_out), .in5(bit_extender_1_out),
    .in9(bit_extender_1_out), .out(Offset), .sel(OpCode));  // open: in0, in1, in6, in7, in8, in10, in11, in12, in13, in14, in15
endmodule
