// Logisim project BOB2200-pipeline.circ as structural Verilog: 11 circuits, main circuit main
module main (
);

  wire BNE_JALR, BranchBit, Chooser, CLK, Comp, CondType, decoder_1_out4, decoder_2_out0, decoder_2_out1,
       decoder_2_out2, decoder_2_out3, decoder_2_out6, decoder_2_out8, decoder_2_out9, Flush, RST, Stall,
       WrEN;
  wire [1:0] Branch, Func;
  wire [3:0] Chosen, EX_MEM_Buffer_opcode_2, IDRR_BUFFER_opcode_2, multiplexer_7_out, multiplexer_11_out,
       Opcode, Opcode_WB, Rx, Rx_E, Rx_M, Ry, WBReg;
  wire [7:0] register_1_q_2;
  wire [19:0] Offset;
  wire [23:0] register_1_q;
  wire [31:0] A, A_E, adder_1_out, ALU, ALU_M, ALU_WB, B, B_E, bit_extender_1_out, bit_extender_2_out,
       Branched_PC, Comp_M, Comp_WB, IFETCH_BUFFER_ir_2, IFETCH_BUFFER_pc_2, MEMValue_WB, multiplexer_1_out,
       multiplexer_2_out, multiplexer_3_out, multiplexer_4_out, multiplexer_5_out, multiplexer_8_out,
       multiplexer_9_out, multiplexer_10_out, multiplexer_12_out, multiplexer_13_out, Offset_E, PC_E,
       PC_Offset, PC_Offset_M, PC_Offset_WB, ram_1_data, ram_2_data, SWData, WBIn;

  Register #(.width(32)) register_1 (
    .D(multiplexer_1_out), .en(1'b1), .Q({register_1_q_2, register_1_q}), .clk(CLK), .clr(RST));
  Clock CLOCK (.out(CLK));
  Button RESET (.out(RST));
  Adder #(.width(32)) adder_1 (.a({register_1_q_2, register_1_q}), .b(32'h1), .out(adder_1_out));  // open: cin, cout
  Multiplexer #(.width(32), .disabled(0), .enable("false")) multiplexer_1 (
    .in0(multiplexer_2_out), .in1(Branched_PC), .out(multiplexer_1_out), .sel(BranchBit));
  Multiplexer #(.width(32), .disabled(0), .enable("false")) multiplexer_2 (
    .in0(adder_1_out), .in1({register_1_q_2, register_1_q}), .out(multiplexer_2_out), .sel(Stall));
  RAM #(.addrWidth(24), .dataWidth(32), .bus("separate")) ram_1 (
    .addr(register_1_q), .data(ram_1_data), .str(1'b0), .sel(1'b1), .clk(CLK), .ld(1'b1), .clr(RST));  // open: din
  Multiplexer #(.width(32), .disabled(0), .enable("false")) multiplexer_3 (
    .in0(multiplexer_2_out), .in1({32{1'b0}}), .out(multiplexer_3_out), .sel(Flush));
  Multiplexer #(.width(32), .disabled(0), .enable("false")) multiplexer_4 (
    .in0(ram_1_data), .in1({32{1'b0}}), .out(multiplexer_4_out), .sel(Flush));
  IF_IDRR_Buffer IFETCH_BUFFER (
    .RST(RST), .CLK(CLK), .PC(multiplexer_3_out), .IR(multiplexer_4_out), .PC_2(IFETCH_BUFFER_pc_2),
    .IR_2(IFETCH_BUFFER_ir_2), .Stall(Stall));
  Multiplexer #(.width(32), .disabled(0), .enable("false")) multiplexer_5 (
    .in0(IFETCH_BUFFER_pc_2), .in1({32{1'b0}}), .out(multiplexer_5_out), .sel(Flush));
  Multiplexer #(.width(32), .disabled(0), .enable("false")) multiplexer_6 (
    .in0(IFETCH_BUFFER_ir_2), .in1({32{1'b0}}), .out({Opcode, Rx, Ry, Offset}), .sel(Flush));
  BChooser BChooser (.Rx(Rx), .Rz(Offset[3:0]), .Opcode(Opcode), .Chosen(Chosen));
  assign bit_extender_1_out = {{12{Offset[19]}}, Offset};  // Bit_Extender bit_extender_1
  Stalling_Unit stalling_unit_1 (.SR1(Ry), .SR2(Chosen), .Stall(Stall), .Rx_E(Rx_E), .Rx_M(Rx_M), .Rx_WB(WBReg));
  Dual_Ported_Register_File dual_ported_register_file_1 (
    .CLK(CLK), .WrREGNO(WBReg), .RdREGNO1(Ry), .RdREGNO2(Chosen), .INPUT(WBIn), .OUT1(A), .OUT2(B),
    .WrEN(WrEN));
  Multiplexer #(.width(4), .disabled(0), .enable("false")) multiplexer_7 (
    .in0(Rx), .in1(4'b0000), .out(multiplexer_7_out), .sel(Stall));
  Multiplexer #(.width(32), .disabled(0), .enable("false")) multiplexer_8 (
    .in0(A), .in1({32{1'b0}}), .out(multiplexer_8_out), .sel(Stall));
  Multiplexer #(.width(32), .disabled(0), .enable("false")) multiplexer_9 (
    .in0(B), .in1({32{1'b0}}), .out(multiplexer_9_out), .sel(Stall));
  Multiplexer #(.width(32), .disabled(0), .enable("false")) multiplexer_10 (
    .in0(bit_extender_1_out), .in1({32{1'b0}}), .out(multiplexer_10_out), .sel(Stall));
  Multiplexer #(.width(4), .disabled(0), .enable("false")) multiplexer_11 (
    .in0(Opcode), .in1(4'b0000), .out(multiplexer_11_out), .sel(Stall));
  Multiplexer #(.width(32), .disabled(0), .enable("false")) multiplexer_12 (
    .in0(multiplexer_5_out), .in1({32{1'b0}}), .out(multiplexer_12_out), .sel(Stall));
  IDRR_EX_Buffer IDRR_BUFFER (
    .PC(multiplexer_12_out), .Rx(multiplexer_7_out), .A(multiplexer_8_out), .B(multiplexer_9_out),
    .Offset(multiplexer_10_out), .Opcode(multiplexer_11_out), .CLK(CLK), .RST(RST), .PC_2(PC_E), .Rx_2(Rx_E),
    .A_2(A_E), .B_2(B_E), .Offset_2(Offset_E), .Opcode_2(IDRR_BUFFER_opcode_2));
  Multiplexer #(.width(32), .disabled(0), .enable("false")) multiplexer_13 (
    .in0(B_E), .in1(Offset_E), .out(multiplexer_13_out), .sel(Chooser));
  Multiplexer #(.width(32), .disabled(0), .enable("false")) multiplexer_14 (
    .in0(PC_Offset), .in1(A_E), .out(Branched_PC), .sel(BNE_JALR));
  Adder #(.width(32)) adder_2 (.a(PC_E), .b(Offset_E), .out(PC_Offset));  // open: cin, cout
  ALU u_ALU (.A(A_E), .B(multiplexer_13_out), .Select(Func), .Output(ALU));
  CompLogic CompLogic (.\output (Comp), .\input (ALU), .mode(CondType));
  Flushing_Unit Flushing_Unit (.BranchSgnl(Branch), .CmpSgnl(Comp), .Flush(Flush));
  Multiplexer #(.select(2), .disabled(0), .enable("false")) multiplexer_15 (
    .in0(1'b0), .in1(1'b1), .in2(Comp), .out(BranchBit), .sel(Branch));  // open: in3
  ROM #(.addrWidth(4), .dataWidth(7)) rom_1 (
    .addr(IDRR_BUFFER_opcode_2), .data({Chooser, BNE_JALR, Branch, CondType, Func}));  // open: sel
  assign bit_extender_2_out = {{31{1'b0}}, Comp};  // Bit_Extender bit_extender_2
  EX_MEM_Buffer EX_MEM_Buffer (
    .PC_Offset(PC_Offset), .Rx(Rx_E), .ALU(ALU), .Comp(bit_extender_2_out), .SWData(B_E),
    .Opcode(IDRR_BUFFER_opcode_2), .CLK(CLK), .RST(RST), .PC_Offset_2(PC_Offset_M), .Rx_2(Rx_M),
    .ALU_2(ALU_M), .Comp_2(Comp_M), .SWData_2(SWData), .Opcode_2(EX_MEM_Buffer_opcode_2));
  Decoder #(.select(4), .enable("false")) decoder_1 (
    .out4(decoder_1_out4), .sel(EX_MEM_Buffer_opcode_2));  // open: out0, out1, out2, out3, out5, out6, out7, out8, out9, out10, out11, out12, out13, out14, out15
  RAM #(.addrWidth(24), .dataWidth(32), .bus("separate")) ram_2 (
    .addr(ALU_M[23:0]), .din(SWData), .data(ram_2_data), .str(decoder_1_out4), .sel(1'b1), .clk(CLK),
    .ld(1'b1), .clr(RST));
  MEM_WB_Buffer WB_BUFFER (
    .PC_Offset(PC_Offset_M), .MEMValue(ram_2_data), .ALU(ALU_M), .Comp(Comp_M),
    .Opcode(EX_MEM_Buffer_opcode_2), .Rx(Rx_M), .CLK(CLK), .RST(RST), .PC_Offset_2(PC_Offset_WB),
    .MEMValue_2(MEMValue_WB), .ALU_2(ALU_WB), .Comp_2(Comp_WB), .Opcode_2(Opcode_WB), .Rx_2(WBReg));
  Decoder #(.select(4), .enable("false")) decoder_2 (
    .out0(decoder_2_out0), .out1(decoder_2_out1), .out2(decoder_2_out2), .out3(decoder_2_out3),
    .out6(decoder_2_out6), .out8(decoder_2_out8), .out9(decoder_2_out9), .sel(Opcode_WB));  // open: out4, out5, out7, out10, out11, out12, out13, out14, out15
  Multiplexer #(.select(4), .width(32), .disabled(0), .enable("false")) multiplexer_16 (
    .in0(ALU_WB), .in1(ALU_WB), .in2(ALU_WB), .in3(MEMValue_WB), .in6(PC_Offset_WB), .in8(Comp_WB),
    .in9(PC_Offset_WB), .out(WBIn), .sel(Opcode_WB));  // open: in4, in5, in7, in10, in11, in12, in13, in14, in15
  or or_1 (WrEN, decoder_2_out0, decoder_2_out1, decoder_2_out2, decoder_2_out3, decoder_2_out6, decoder_2_out8, decoder_2_out9);

  // Other names for the same wires on the sheet: Rz[3:0] = Offset[3:0]

  // Notes on the sheet:
  //   contents of rom_1 (hex, n*v repeats v):
  //   0 2 40 40 40 11 28 18 5
endmodule

module Dual_Ported_Register_File (
  input  CLK,
  input  WrEN,
  input  [3:0] WrREGNO,
  input  [3:0] RdREGNO1,
  input  [3:0] RdREGNO2,
  input  [31:0] INPUT,
  output [31:0] OUT1,
  output [31:0] OUT2
);

  wire En_a0, En_a1, En_a2, En_at, En_fp, En_k0, En_ra, En_s0, En_s1, En_s2, En_sp, En_t0, En_t1, En_t2,
       En_v0;
  wire [31:0] a0, a1, a2, at, fp, k0, ra, s0, s1, s2, sp, t0, t1, t2, v0, zero;

  Decoder #(.select(4), .disabled(0)) decoder_1 (
    .out1(En_at), .out2(En_v0), .out3(En_a0), .out4(En_a1), .out5(En_a2), .out6(En_t0), .out7(En_t1),
    .out8(En_t2), .out9(En_s0), .out10(En_s1), .out11(En_s2), .out12(En_k0), .out13(En_sp), .out14(En_fp),
    .out15(En_ra), .sel(WrREGNO), .en(WrEN));  // open: out0
  Register #(.width(32)) u_zero (.D(INPUT), .en(1'b0), .Q(zero), .clk(CLK));  // open: clr
  Register #(.width(32)) u_at (.D(INPUT), .en(En_at), .Q(at), .clk(CLK));  // open: clr
  Register #(.width(32)) u_v0 (.D(INPUT), .en(En_v0), .Q(v0), .clk(CLK));  // open: clr
  Register #(.width(32)) u_a0 (.D(INPUT), .en(En_a0), .Q(a0), .clk(CLK));  // open: clr
  Register #(.width(32)) u_a1 (.D(INPUT), .en(En_a1), .Q(a1), .clk(CLK));  // open: clr
  Register #(.width(32)) u_a2 (.D(INPUT), .en(En_a2), .Q(a2), .clk(CLK));  // open: clr
  Register #(.width(32)) u_t0 (.D(INPUT), .en(En_t0), .Q(t0), .clk(CLK));  // open: clr
  Register #(.width(32)) u_t1 (.D(INPUT), .en(En_t1), .Q(t1), .clk(CLK));  // open: clr
  Multiplexer #(.select(4), .width(32), .disabled(0), .enable("false")) multiplexer_1 (
    .in0(zero), .in1(at), .in2(v0), .in3(a0), .in4(a1), .in5(a2), .in6(t0), .in7(t1), .in8(t2), .in9(s0),
    .in10(s1), .in11(s2), .in12(k0), .in13(sp), .in14(fp), .in15(ra), .out(OUT2), .sel(RdREGNO2));
  Register #(.width(32)) u_t2 (.D(INPUT), .en(En_t2), .Q(t2), .clk(CLK));  // open: clr
  Register #(.width(32)) u_s0 (.D(INPUT), .en(En_s0), .Q(s0), .clk(CLK));  // open: clr
  Register #(.width(32)) u_s1 (.D(INPUT), .en(En_s1), .Q(s1), .clk(CLK));  // open: clr
  Register #(.width(32)) u_s2 (.D(INPUT), .en(En_s2), .Q(s2), .clk(CLK));  // open: clr
  Register #(.width(32)) u_k0 (.D(INPUT), .en(En_k0), .Q(k0), .clk(CLK));  // open: clr
  Register #(.width(32)) u_sp (.D(INPUT), .en(En_sp), .Q(sp), .clk(CLK));  // open: clr
  Register #(.width(32)) u_fp (.D(INPUT), .en(En_fp), .Q(fp), .clk(CLK));  // open: clr
  Register #(.width(32)) u_ra (.D(INPUT), .en(En_ra), .Q(ra), .clk(CLK));  // open: clr
  Multiplexer #(.select(4), .width(32), .disabled(0), .enable("false")) multiplexer_2 (
    .in0(zero), .in1(at), .in2(v0), .in3(a0), .in4(a1), .in5(a2), .in6(t0), .in7(t1), .in8(t2), .in9(s0),
    .in10(s1), .in11(s2), .in12(k0), .in13(sp), .in14(fp), .in15(ra), .out(OUT1), .sel(RdREGNO1));

  // Notes on the sheet:
  //   MODIFY AT YOUR OWN RISK
endmodule

module IF_IDRR_Buffer (
  input  RST,
  input  CLK,
  input  [31:0] PC,
  input  [31:0] IR,
  input  Stall,
  output [31:0] PC_2,
  output [31:0] IR_2
);

  wire Enable;

  Register #(.width(32)) u_PC (.D(PC), .en(Enable), .Q(PC_2), .clk(CLK), .clr(RST));
  Register #(.width(32)) u_IR (.D(IR), .en(Enable), .Q(IR_2), .clk(CLK), .clr(RST));
  not not_1 (Enable, Stall);
endmodule

module IDRR_EX_Buffer (
  input  [31:0] PC,
  input  [3:0] Rx,
  input  [31:0] A,
  input  [31:0] B,
  input  [31:0] Offset,
  input  [3:0] Opcode,
  input  CLK,
  input  RST,
  output [31:0] PC_2,
  output [3:0] Rx_2,
  output [31:0] A_2,
  output [31:0] B_2,
  output [31:0] Offset_2,
  output [3:0] Opcode_2
);

  Register #(.width(32)) u_PC (.D(PC), .en(1'b1), .Q(PC_2), .clk(CLK), .clr(RST));
  Register #(.width(4)) u_Rx (.D(Rx), .en(1'b1), .Q(Rx_2), .clk(CLK), .clr(RST));
  Register #(.width(32)) u_A (.D(A), .en(1'b1), .Q(A_2), .clk(CLK), .clr(RST));
  Register #(.width(32)) u_B (.D(B), .en(1'b1), .Q(B_2), .clk(CLK), .clr(RST));
  Register #(.width(32)) u_Offset (.D(Offset), .en(1'b1), .Q(Offset_2), .clk(CLK), .clr(RST));
  Register #(.width(4)) u_Opcode (.D(Opcode), .en(1'b1), .Q(Opcode_2), .clk(CLK), .clr(RST));
endmodule

module EX_MEM_Buffer (
  input  [31:0] PC_Offset,
  input  [3:0] Rx,
  input  [31:0] ALU,
  input  [31:0] Comp,
  input  [31:0] SWData,
  input  [3:0] Opcode,
  input  CLK,
  input  RST,
  output [31:0] PC_Offset_2,
  output [3:0] Rx_2,
  output [31:0] ALU_2,
  output [31:0] Comp_2,
  output [31:0] SWData_2,
  output [3:0] Opcode_2
);

  Register #(.width(32)) u_PC_Offset (.D(PC_Offset), .en(1'b1), .Q(PC_Offset_2), .clk(CLK), .clr(RST));
  Register #(.width(4)) u_Rx (.D(Rx), .en(1'b1), .Q(Rx_2), .clk(CLK), .clr(RST));
  Register #(.width(32)) u_ALU (.D(ALU), .en(1'b1), .Q(ALU_2), .clk(CLK), .clr(RST));
  Register #(.width(32)) u_Comp (.D(Comp), .en(1'b1), .Q(Comp_2), .clk(CLK), .clr(RST));
  Register #(.width(32)) u_SWData (.D(SWData), .en(1'b1), .Q(SWData_2), .clk(CLK), .clr(RST));
  Register #(.width(4)) u_Opcode (.D(Opcode), .en(1'b1), .Q(Opcode_2), .clk(CLK), .clr(RST));
endmodule

module MEM_WB_Buffer (
  input  [31:0] PC_Offset,
  input  [31:0] MEMValue,
  input  [31:0] ALU,
  input  [31:0] Comp,
  input  [3:0] Opcode,
  input  [3:0] Rx,
  input  CLK,
  input  RST,
  output [31:0] PC_Offset_2,
  output [31:0] MEMValue_2,
  output [31:0] ALU_2,
  output [31:0] Comp_2,
  output [3:0] Opcode_2,
  output [3:0] Rx_2
);

  Register #(.width(32)) u_PC_Offset (.D(PC_Offset), .en(1'b1), .Q(PC_Offset_2), .clk(CLK), .clr(RST));
  Register #(.width(32)) u_MEMValue (.D(MEMValue), .en(1'b1), .Q(MEMValue_2), .clk(CLK), .clr(RST));
  Register #(.width(32)) u_ALU (.D(ALU), .en(1'b1), .Q(ALU_2), .clk(CLK), .clr(RST));
  Register #(.width(32)) u_Comp (.D(Comp), .en(1'b1), .Q(Comp_2), .clk(CLK), .clr(RST));
  Register #(.width(4)) u_Opcode (.D(Opcode), .en(1'b1), .Q(Opcode_2), .clk(CLK), .clr(RST));
  Register #(.width(4)) u_Rx (.D(Rx), .en(1'b1), .Q(Rx_2), .clk(CLK), .clr(RST));
endmodule

module BChooser (
  input  [3:0] Rx,
  input  [3:0] Rz,
  input  [3:0] Opcode,
  output [3:0] Chosen
);

  Multiplexer #(.select(4), .width(4), .disabled(0), .enable("false")) multiplexer_1 (
    .in0(Rz), .in1(Rz), .in4(Rx), .in5(Rx), .in8(Rz), .out(Chosen), .sel(Opcode));  // open: in2, in3, in6, in7, in9, in10, in11, in12, in13, in14, in15
endmodule

module ALU (
  input  [31:0] A,
  input  [31:0] B,
  input  [1:0] Select,
  output [31:0] Output
);

  wire [31:0] adder_1_out, adder_2_out, nand_1_out, subtractor_1_out;

  Adder #(.width(32)) adder_1 (.a(A), .b(B), .out(adder_1_out));  // open: cin, cout
  Subtractor #(.width(32)) subtractor_1 (.a(A), .b(B), .out(subtractor_1_out));  // open: bin, bout
  assign nand_1_out = ~(A & B);  // NAND_Gate nand_1, 32 bits wide
  Adder #(.width(32)) adder_2 (.a(A), .b({32{1'b0}}), .out(adder_2_out), .cin(1'b1));  // open: cout
  // Probe on adder_1_out
  // Probe on subtractor_1_out
  // Probe on nand_1_out
  Multiplexer #(.select(2), .width(32), .disabled(0), .enable("false")) multiplexer_1 (
    .in0(adder_1_out), .in1(subtractor_1_out), .in2(nand_1_out), .in3(adder_2_out), .out(Output), .sel(Select));
endmodule

module CompLogic (
  input  [31:0] \input ,
  input  mode,
  output \output 
);

  wire comparator_1_eq, comparator_1_lt, not_1_out;

  Comparator #(.width(32)) comparator_1 (
    .a(\input ), .b({32{1'b0}}), .eq(comparator_1_eq), .lt(comparator_1_lt));  // open: gt
  Multiplexer #(.disabled(0), .enable("false")) multiplexer_1 (
    .in0(not_1_out), .in1(comparator_1_lt), .out(\output ), .sel(mode));
  not not_1 (not_1_out, comparator_1_eq);
  Pull_Resistor pull_resistor_1 (.node(\output ));
endmodule

module Flushing_Unit (
  input  [1:0] BranchSgnl,
  input  CmpSgnl,
  output Flush
);

  wire and_1_out;

  and and_1 (and_1_out, BranchSgnl[1], CmpSgnl);
  or or_1 (Flush, BranchSgnl[0], and_1_out);

  // Other names for the same wires on the sheet: Bit0 = BranchSgnl[0]; Bit1 = BranchSgnl[1]
endmodule

module Stalling_Unit (
  input  [3:0] Rx_E,
  input  [3:0] Rx_M,
  input  [3:0] Rx_WB,
  input  [3:0] SR1,
  input  [3:0] SR2,
  output Stall
);

  wire and_1_out, and_2_out, comparator_1_eq, comparator_2_eq, comparator_3_eq, comparator_4_eq,
       comparator_5_eq, comparator_6_eq, comparator_7_eq, comparator_8_eq, not_1_out, not_2_out, or_1_out,
       or_2_out;

  Comparator #(.width(4), .mode("unsigned")) comparator_1 (.a(Rx_E), .b(SR1), .eq(comparator_1_eq));  // open: gt, lt
  Comparator #(.width(4), .mode("unsigned")) comparator_2 (.a(Rx_E), .b(SR2), .eq(comparator_2_eq));  // open: gt, lt
  Comparator #(.width(4), .mode("unsigned")) comparator_3 (.a(Rx_M), .b(SR1), .eq(comparator_3_eq));  // open: gt, lt
  Comparator #(.width(4), .mode("unsigned")) comparator_4 (.a(Rx_M), .b(SR2), .eq(comparator_4_eq));  // open: gt, lt
  Comparator #(.width(4), .mode("unsigned")) comparator_5 (.a(Rx_WB), .b(SR1), .eq(comparator_5_eq));  // open: gt, lt
  Comparator #(.width(4), .mode("unsigned")) comparator_6 (.a(Rx_WB), .b(SR2), .eq(comparator_6_eq));  // open: gt, lt
  Comparator #(.width(4), .mode("unsigned")) comparator_7 (.a(SR1), .b(4'b0000), .eq(comparator_7_eq));  // open: gt, lt
  Comparator #(.width(4), .mode("unsigned")) comparator_8 (.a(SR2), .b(4'b0000), .eq(comparator_8_eq));  // open: gt, lt
  not not_1 (not_1_out, comparator_7_eq);
  or or_1 (or_1_out, comparator_5_eq, comparator_3_eq, comparator_1_eq);
  or or_2 (or_2_out, comparator_6_eq, comparator_4_eq, comparator_2_eq);
  not not_2 (not_2_out, comparator_8_eq);
  and and_1 (and_1_out, not_1_out, or_1_out);
  and and_2 (and_2_out, or_2_out, not_2_out);
  or or_3 (Stall, and_1_out, and_2_out);
  Pull_Resistor pull_resistor_1 (.node(Stall));
endmodule
